# Fritzing sketch fritzing_arch (saved by Fritzing 1.0.0rc)

parts:
  U1 = LuaNode32 / ESP32 [part_number=ESP32S-PIN30]
  DHT11_1 = DHT11 module
  U2 = LuaNode32 / ESP32 [part_number=ESP32S-PIN30]
  DHT11_2 = DHT11 module
  U3 = LuaNode32 / ESP32 [part_number=ESP32S-PIN30]  # not connected

nets:
  3V3: U1.3V3, DHT11_1.VCC
  GND: U1.GND, DHT11_1.GND
  N1: U1.D5, DHT11_1.DATA
  3V3_2: U2.3V3, DHT11_2.VCC
  GND_2: U2.GND, DHT11_2.GND
  N2: U2.D5, DHT11_2.DATA

notes:
  lave 1<module fritzingVersion="1.0.0rc.2023-06-02.CD-4157-0-6b14cfe9">
  <boundingRects>
  <boundingRect name="PCB View" rect="0 0 0 0"/>
  <boundingRect name="Breadboard View" rect="217.041 -48.8119 163.931 268.409"/>
  <boundingRect name="Schematic View" rect="0 0 0 0"/>
  </boundingRects>
  <instances>
  <instance modelIndex="85516618" path="C:/Users/dvelas25/Documents/Fritzing/parts/user/LuaNode32_ESP32_r1_586998f444d5fd7ff874a07d13809fb5_3.fzp" moduleIdRef="LuaNode32_ESP32_r1_586998f444d5fd7ff874a07d13809fb5_3">
  <property name="part number" value="ESP32S-PIN30"/>
  <title>U1</title>
  <views>
  <breadboardView layer="breadboard">
  <geometry z="2.5" y="78.0515" x="239.427">
  <transform m22="0" m11="0" m21="-1" m33="1" m31="141.545" m13="0" m12="1" m32="-41.0196" m23="0"/>
  </geometry>
  <connectors>
  <connector layer="breadboard" connectorId="connector16">
  <geometry y="0" x="0"/>
  <connects>
  <connect layer="breadboardWire" modelIndex="85516624" connectorId="connector0"/>
  </connects>
  </connector>
  <connector layer="breadboard" connectorId="connector15">
  <geometry y="0" x="0"/>
  <connects>
  <connect layer="breadboardWire" modelIndex="85516638" connectorId="connector0"/>
  </connects>
  </connector>
  <connector layer="breadboard" connectorId="connector35">
  <geometry y="0" x="0"/>
  <connects>
  <connect layer="breadboardWire" modelIndex="85516652" connectorId="connector0"/>
  </connects>
  </connector>
  </connectors>
  </breadboardView>
  <schematicView layer="schematic">
  <geometry z="2.5" y="7.73378" x="188.514"/>
  <titleGeometry z="6.5" xOffset="81.25" visible="true" y="-6.26622" x="269.764" textColor="#000000" yOffset="-14" fontSize="5">
  <displayKey key=""/>
  <displayKey key="mn"/>
  <displayKey key="mpn"/>
  <displayKey key="part number"/>
  </titleGeometry>
  <connectors>
  <connector layer="schematic" connectorId="connector16">
  <geometry y="0" x="0"/>
  <connects>
  <connect layer="schematicTrace" modelIndex="85516624" connectorId="connector0"/>
  </connects>
  </connector>
  <connector layer="schematic" connectorId="connector15">
  <geometry y="0" x="0"/>
  <connects>
  <connect layer="schematicTrace" modelIndex="85516638" connectorId="connector0"/>
  </connects>
  </connector>
  <connector layer="schematic" connectorId="connector35">
  <geometry y="0" x="0"/>
  <connects>
  <connect layer="schematicTrace" modelIndex="85516652" connectorId="connector0"/>
  </connects>
  </connector>
  </connectors>
  </schematicView>
  <pcbView layer="copper0">
  <geometry z="5.5" y="21.5266" x="62.1657"/>
  <titleGeometry z="12.5" xOffset="184.746" visible="true" y="14.5266" x="246.912" textColor="#000000" yOffset="-7" fontSize="5">
  <displayKey key=""/>
  </titleGeometry>
  <connectors>
  <connector layer="copper0" connectorId="connector16">
  <geometry y="0" x="0"/>
  <connects>
  <connect layer="copper1trace" modelIndex="85516624" connectorId="connector0"/>
  </connects>
  </connector>
  <connector layer="copper0" connectorId="connector15">
  <geometry y="0" x="0"/>
  <connects>
  <connect layer="copper1trace" modelIndex="85516638" connectorId="connector0"/>
  </connects>
  </connector>
  <connector layer="copper0" connectorId="connector35">
  <geometry y="0" x="0"/>
  <connects>
  <connect layer="copper1trace" modelIndex="85516652" connectorId="connector0"/>
  </connects>
  </connector>
  </connectors>
  </pcbView>
  </views>
  </instance>
  <instance modelIndex="85516621" path="C:/Users/dvelas25/Documents/Fritzing/parts/user/DHT22_BLACK_PCB_8f30cda20dc2ef169d377f5ee20d1d5d_6.fzp" moduleIdRef="DHT22_BLACK_PCB_8f30cda20dc2ef169d377f5ee20d1d5d_6">
  <title>DHT11 1</title>
  <views>
  <breadboardView layer="breadboard">
  <geometry z="2.50001" y="-48.8119" x="217.041"/>
  <connectors>
  <connector layer="breadboard" connectorId="connector6">
  <geometry y="0" x="0"/>
  <connects>
  <connect layer="breadboardWire" modelIndex="85516631" connectorId="connector1"/>
  </connects>
  </connector>
  <connector layer="breadboard" connectorId="connector5">
  <geometry y="0" x="0"/>
  <connects>
  <connect layer="breadboardWire" modelIndex="85516645" connectorId="connector1"/>
  </connects>
  </connector>
  <connector layer="breadboard" connectorId="connector9">
  <geometry y="0" x="0"/>
  <connects>
  <connect layer="breadboardWire" modelIndex="85516659" connectorId="connector1"/>
  </connects>
  </connector>
  </connectors>
  </breadboardView>
  <schematicView layer="schematic">
  <geometry z="2.5" y="-42.5442" x="494.019"/>
  <titleGeometry z="6.50001" xOffset="456.294" visible="true" y="-49.5442" x="950.313" textColor="#000000" yOffset="-7" fontSize="5">
  <displayKey key=""/>
  <displayKey key="mn"/>
  <displayKey key="mpn"/>
  <displayKey key="part number"/>
  </titleGeometry>
  <connectors>
  <connector layer="schematic" connectorId="connector6">
  <geometry y="0" x="0"/>
  <connects>
  <connect layer="schematicTrace" modelIndex="85516631" connectorId="connector1"/>
  </connects>
  </connector>
  <connector layer="schematic" connectorId="connector5">
  <geometry y="0" x="0"/>
  <connects>
  <connect layer="schematicTrace" modelIndex="85516645" connectorId="connector1"/>
  </connects>
  </connector>
  <connector layer="schematic" connectorId="connector9">
  <geometry y="0" x="0"/>
  <connects>
  <connect layer="schematicTrace" modelIndex="85516659" connectorId="connector1"/>
  </connects>
  </connector>
  </connectors>
  </schematicView>
  <pcbView layer="copper1">
  <geometry z="8.50001" y="26.9792" x="268.566"/>
  <titleGeometry z="12.5" xOffset="36" visible="true" y="19.9792" x="304.566" textColor="#000000" yOffset="-7" fontSize="5">
  <displayKey key=""/>
  </titleGeometry>
  <connectors>
  <connector layer="copper1" connectorId="connector6">
  <geometry y="0" x="0"/>
  <connects>
  <connect layer="copper1trace" modelIndex="85516631" connectorId="connector1"/>
  </connects>
  </connector>
  <connector layer="copper1" connectorId="connector5">
  <geometry y="0" x="0"/>
  <connects>
  <connect layer="copper1trace" modelIndex="85516645" connectorId="connector1"/>
  </connects>
  </connector>
  <connector layer="copper1" connectorId="connector9">
  <geometry y="0" x="0"/>
  <connects>
  <connect layer="copper1trace" modelIndex="85516659" connectorId="connector1"/>
  </connects>
  </connector>
  </connectors>
  </pcbView>
  </views>
  </instance>
  <instance modelIndex="85516631" path=":/resources/parts/core/wire.fzp" moduleIdRef="WireModuleID">
  <title>Wire4</title>
  <views>
  <breadboardView layer="breadboardWire">
  <geometry x2="-0.0207692" z="3.5" y="80.846" x="258.771" y2="-15.596" y1="0" x1="0" wireFlags="64"/>
  <wireExtras mils="22.2222" banded="0" opacity="1" color="#404040"/>
  <connectors>
  <connector layer="breadboardWire" connectorId="connector1">
  <geometry y="0" x="0"/>
  <connects>
  <connect layer="breadboard" modelIndex="85516621" connectorId="connector6"/>
  </connects>
  </connector>
  <connector layer="breadboardWire" connectorId="connector0">
  <geometry y="0" x="0"/>
  <connects>
  <connect layer="breadboardWire" modelIndex="85516624" connectorId="connector1"/>
  </connects>
  </connector>
  </connectors>
  </breadboardView>
  <schematicView layer="schematicTrace">
  <geometry x2="-0.0207692" z="5.50001" y="80.846" x="258.771" y2="-15.596" y1="0" x1="0" wireFlags="64"/>
  <wireExtras mils="9.7222" banded="0" opacity="1" color="#404040"/>
  <connectors>
  <connector layer="schematicTrace" connectorId="connector1">
  <geometry y="0" x="0"/>
  <connects>
  <connect layer="schematic" modelIndex="85516621" connectorId="connector6"/>
  </connects>
  </connector>
  <connector layer="schematicTrace" connectorId="connector0">
  <geometry y="0" x="0"/>
  <connects>
  <connect layer="schematicTrace" modelIndex="85516624" connectorId="connector1"/>
  </connects>
  </connector>
  </connectors>
  </schematicView>
  <pcbView layer="copper1trace">
  <geometry x2="-0.0207692" z="9.50001" y="80.846" x="258.771" y2="-15.596" y1="0" x1="0" wireFlags="64"/>
  <wireExtras mils="11.1111" banded="0" opacity="1" color="#f2c600"/>
  <connectors>
  <connector layer="copper1trace" connectorId="connector1">
  <geometry y="0" x="0"/>
  <connects>
  <connect layer="copper1" modelIndex="85516621" connectorId="connector6"/>
  </connects>
  </connector>
  <connector layer="copper1trace" connectorId="connector0">
  <geometry y="0" x="0"/>
  <connects>
  <connect layer="copper1trace" modelIndex="85516624" connectorId="connector1"/>
  </connects>
  </connector>
  </connectors>
  </pcbView>
  </views>
  </instance>
  <instance modelIndex="85516624" path=":/resources/parts/core/wire.fzp" moduleIdRef="WireModuleID">
  <title>Wire1</title>
  <views>
  <breadboardView layer="breadboardWire">
  <geometry x2="-26.925" z="3.5" y="80.8907" x="285.696" y2="-0.0447768" y1="0" x1="0" wireFlags="64"/>
  <wireExtras mils="22.2222" banded="0" opacity="1" color="#404040"/>
  <connectors>
  <connector layer="breadboardWire" connectorId="connector1">
  <geometry y="0" x="0"/>
  <connects>
  <connect layer="breadboardWire" modelIndex="85516631" connectorId="connector0"/>
  </connects>
  </connector>
  <connector layer="breadboardWire" connectorId="connector0">
  <geometry y="0" x="0"/>
  <connects>
  <connect layer="breadboard" modelIndex="85516618" connectorId="connector16"/>
  </connects>
  </connector>
  </connectors>
  </breadboardView>
  <schematicView layer="schematicTrace">
  <geometry x2="-58.8839" z="5.5" y="82.1191" x="317.973" y2="-15.5963" y1="0" x1="0" wireFlags="64"/>
  <wireExtras mils="9.7222" banded="0" opacity="1" color="#404040"/>
  <connectors>
  <connector layer="schematicTrace" connectorId="connector1">
  <geometry y="0" x="0"/>
  <connects>
  <connect layer="schematicTrace" modelIndex="85516631" connectorId="connector0"/>
  </connects>
  </connector>
  <connector layer="schematicTrace" connectorId="connector0">
  <geometry y="0" x="0"/>
  <connects>
  <connect layer="schematic" modelIndex="85516618" connectorId="connector16"/>
  </connects>
  </connector>
  </connectors>
  </schematicView>
  <pcbView layer="copper1trace">
  <geometry x2="-58.8839" z="9.5" y="82.1191" x="317.973" y2="-15.5963" y1="0" x1="0" wireFlags="64"/>
  <wireExtras mils="11.1111" banded="0" opacity="1" color="#f2c600"/>
  <connectors>
  <connector layer="copper1trace" connectorId="connector1">
  <geometry y="0" x="0"/>
  <connects>
  <connect layer="copper1trace" modelIndex="85516631" connectorId="connector0"/>
  </connects>
  </connector>
  <connector layer="copper1trace" connectorId="connector0">
  <geometry y="0" x="0"/>
  <connects>
  <connect layer="copper0" modelIndex="85516618" connectorId="connector16"/>
  </connects>
  </connector>
  </connectors>
  </pcbView>
  </views>
  </instance>
  <instance modelIndex="85516645" path=":/resources/parts/core/wire.fzp" moduleIdRef="WireModuleID">
  <title>Wire10</title>
  <views>
  <breadboardView layer="breadboardWire">
  <geometry x2="0" z="3.50001" y="71.8831" x="239.548" y2="-6.63303" y1="0" x1="0" wireFlags="64"/>
  <wireExtras mils="22.2222" banded="0" opacity="1" color="#cc1414"/>
  <connectors>
  <connector layer="breadboardWire" connectorId="connector1">
  <geometry y="0" x="0"/>
  <connects>
  <connect layer="breadboard" modelIndex="85516621" connectorId="connector5"/>
  </connects>
  </connector>
  <connector layer="breadboardWire" connectorId="connector0">
  <geometry y="0" x="0"/>
  <connects>
  <connect layer="breadboardWire" modelIndex="85516638" connectorId="connector1"/>
  </connects>
  </connector>
  </connectors>
  </breadboardView>
  <schematicView layer="schematicTrace">
  <geometry x2="1.14759" z="5.50003" y="71.9338" x="238.4" y2="-6.68376" y1="0" x1="0" wireFlags="64"/>
  <wireExtras mils="9.7222" banded="0" opacity="1" color="#404040"/>
  <connectors>
  <connector layer="schematicTrace" connectorId="connector1">
  <geometry y="0" x="0"/>
  <connects>
  <connect layer="schematic" modelIndex="85516621" connectorId="connector5"/>
  </connects>
  </connector>
  <connector layer="schematicTrace" connectorId="connector0">
  <geometry y="0" x="0"/>
  <connects>
  <connect layer="schematicTrace" modelIndex="85516638" connectorId="connector1"/>
  </connects>
  </connector>
  </connectors>
  </schematicView>
  <pcbView layer="copper1trace">
  <geometry x2="1.14759" z="9.50003" y="71.9338" x="238.4" y2="-6.68376" y1="0" x1="0" wireFlags="64"/>
  <wireExtras mils="11.1111" banded="0" opacity="1" color="#f2c600"/>
  <connectors>
  <connector layer="copper1trace" connectorId="connector1">
  <geometry y="0" x="0"/>
  <connects>
  <connect layer="copper1" modelIndex="85516621" connectorId="connector5"/>
  </connects>
  </connector>
  <connector layer="copper1trace" connectorId="connector0">
  <geometry y="0" x="0"/>
  <connects>
  <connect layer="copper1trace" modelIndex="85516638" connectorId="connector1"/>
  </connects>
  </connector>
  </connectors>
  </pcbView>
  </views>
  </instance>
  <instance modelIndex="85516638" path=":/resources/parts/core/wire.fzp" moduleIdRef="WireModuleID">
  <title>Wire7</title>
  <views>
  <breadboardView layer="breadboardWire">
  <geometry x2="-46.1481" z="3.50001" y="71.8831" x="285.696" y2="-2.84217e-14" y1="0" x1="0" wireFlags="64"/>
  <wireExtras mils="22.2222" banded="0" opacity="1" color="#cc1414"/>
  <connectors>
  <connector layer="breadboardWire" connectorId="connector1">
  <geometry y="0" x="0"/>
  <connects>
  <connect layer="breadboardWire" modelIndex="85516645" connectorId="connector0"/>
  </connects>
  </connector>
  <connector layer="breadboardWire" connectorId="connector0">
  <geometry y="0" x="0"/>
  <connects>
  <connect layer="breadboard" modelIndex="85516618" connectorId="connector15"/>
  </connects>
  </connector>
  </connectors>
  </breadboardView>
  <schematicView layer="schematicTrace">
  <geometry x2="-81.1643" z="5.50002" y="73.8436" x="318.61" y2="-9.23045" y1="0" x1="0" wireFlags="64"/>
  <wireExtras mils="9.7222" banded="0" opacity="1" color="#404040"/>
  <connectors>
  <connector layer="schematicTrace" connectorId="connector1">
  <geometry y="0" x="0"/>
  <connects>
  <connect layer="schematicTrace" modelIndex="85516645" connectorId="connector0"/>
  </connects>
  </connector>
  <connector layer="schematicTrace" connectorId="connector0">
  <geometry y="0" x="0"/>
  <connects>
  <connect layer="schematic" modelIndex="85516618" connectorId="connector15"/>
  </connects>
  </connector>
  </connectors>
  </schematicView>
  <pcbView layer="copper1trace">
  <geometry x2="-81.1643" z="9.50002" y="73.8436" x="318.61" y2="-9.23045" y1="0" x1="0" wireFlags="64"/>
  <wireExtras mils="11.1111" banded="0" opacity="1" color="#f2c600"/>
  <connectors>
  <connector layer="copper1trace" connectorId="connector1">
  <geometry y="0" x="0"/>
  <connects>
  <connect layer="copper1trace" modelIndex="85516645" connectorId="connector0"/>
  </connects>
  </connector>
  <connector layer="copper1trace" connectorId="connector0">
  <geometry y="0" x="0"/>
  <connects>
  <connect layer="copper0" modelIndex="85516618" connectorId="connector15"/>
  </connects>
  </connector>
  </connectors>
  </pcbView>
  </views>
  </instance>
  <instance modelIndex="85516659" path=":/resources/parts/core/wire.fzp" moduleIdRef="WireModuleID">
  <title>Wire16</title>
  <views>
  <breadboardView layer="breadboardWire">
  <geometry x2="0" z="3.50002" y="134.952" x="249.149" y2="-69.7017" y1="0" x1="0" wireFlags="64"/>
  <wireExtras mils="22.2222" banded="0" opacity="1" color="#418dd9"/>
  <connectors>
  <connector layer="breadboardWire" connectorId="connector1">
  <geometry y="0" x="0"/>
  <connects>
  <connect layer="breadboard" modelIndex="85516621" connectorId="connector9"/>
  </connects>
  </connector>
  <connector layer="breadboardWire" connectorId="connector0">
  <geometry y="0" x="0"/>
  <connects>
  <connect layer="breadboardWire" modelIndex="85516652" connectorId="connector1"/>
  </connects>
  </connector>
  </connectors>
  </breadboardView>
  <schematicView layer="schematicTrace">
  <geometry x2="0" z="5.50005" y="134.952" x="249.149" y2="-69.7017" y1="0" x1="0" wireFlags="64"/>
  <wireExtras mils="9.7222" banded="0" opacity="1" color="#404040"/>
  <connectors>
  <connector layer="schematicTrace" connectorId="connector1">
  <geometry y="0" x="0"/>
  <connects>
  <connect layer="schematic" modelIndex="85516621" connectorId="connector9"/>
  </connects>
  </connector>
  <connector layer="schematicTrace" connectorId="connector0">
  <geometry y="0" x="0"/>
  <connects>
  <connect layer="schematicTrace" modelIndex="85516652" connectorId="connector1"/>
  </connects>
  </connector>
  </connectors>
  </schematicView>
  <pcbView layer="copper1trace">
  <geometry x2="0" z="9.50005" y="134.952" x="249.149" y2="-69.7017" y1="0" x1="0" wireFlags="64"/>
  <wireExtras mils="11.1111" banded="0" opacity="1" color="#f2c600"/>
  <connectors>
  <connector layer="copper1trace" connectorId="connector1">
  <geometry y="0" x="0"/>
  <connects>
  <connect layer="copper1" modelIndex="85516621" connectorId="connector9"/>
  </connects>
  </connector>
  <connector layer="copper1trace" connectorId="connector0">
  <geometry y="0" x="0"/>
  <connects>
  <connect layer="copper1trace" modelIndex="85516652" connectorId="connector1"/>
  </connects>
  </connector>
  </connectors>
  </pcbView>
  </views>
  </instance>
  <instance modelIndex="85516652" path=":/resources/parts/core/wire.fzp" moduleIdRef="WireModuleID">
  <title>Wire13</title>
  <views>
  <breadboardView layer="breadboardWire">
  <geometry x2="-36.5465" z="3.50002" y="134.952" x="285.696" y2="-2.84217e-14" y1="0" x1="0" wireFlags="64"/>
  <wireExtras mils="22.2222" banded="0" opacity="1" color="#418dd9"/>
  <connectors>
  <connector layer="breadboardWire" connectorId="connector1">
  <geometry y="0" x="0"/>
  <connects>
  <connect layer="breadboardWire" modelIndex="85516659" connectorId="connector0"/>
  </connects>
  </connector>
  <connector layer="breadboardWire" connectorId="connector0">
  <geometry y="0" x="0"/>
  <connects>
  <connect layer="breadboard" modelIndex="85516618" connectorId="connector35"/>
  </connects>
  </connector>
  </connectors>
  </breadboardView>
  <schematicView layer="schematicTrace">
  <geometry x2="-67.2494" z="5.50004" y="133.774" x="316.308" y2="-67.7932" y1="0" x1="0" wireFlags="64"/>
  <wireExtras mils="9.7222" banded="0" opacity="1" color="#404040"/>
  <connectors>
  <connector layer="schematicTrace" connectorId="connector1">
  <geometry y="0" x="0"/>
  <connects>
  <connect layer="schematicTrace" modelIndex="85516659" connectorId="connector0"/>
  </connects>
  </connector>
  <connector layer="schematicTrace" connectorId="connector0">
  <geometry y="0" x="0"/>
  <connects>
  <connect layer="schematic" modelIndex="85516618" connectorId="connector35"/>
  </connects>
  </connector>
  </connectors>
  </schematicView>
  <pcbView layer="copper1trace">
  <geometry x2="-67.2494" z="9.50004" y="133.774" x="316.308" y2="-67.7932" y1="0" x1="0" wireFlags="64"/>
  <wireExtras mils="11.1111" banded="0" opacity="1" color="#f2c600"/>
  <connectors>
  <connector layer="copper1trace" connectorId="connector1">
  <geometry y="0" x="0"/>
  <connects>
  <connect layer="copper1trace" modelIndex="85516659" connectorId="connector0"/>
  </connects>
  </connector>
  <connector layer="copper1trace" connectorId="connector0">
  <geometry y="0" x="0"/>
  <connects>
  <connect layer="copper0" modelIndex="85516618" connectorId="connector35"/>
  </connects>
  </connector>
  </connectors>
  </pcbView>
  </views>
  </instance>
  </instances>
  </module>
  Slave 2
  Master

custom parts:
  LuaNode32 / ESP32: New Image for LuaNode32 DOIT ESP32 DEVKIT V1. Base parts from LuaNode32 / ESP32 ESP32 based LuaNode32 by G.Noorlander DOIT Esp32 DevKit v1 (30 pins long, 11 pins width) by Werner Rothschopf (modified by vanepp Dec 2018)
  DHT11 module: https://cdn-learn.adafruit.com/downloads/pdf/dht.pdf DHT11 black pcb module reference by:https://github.com/adafruit/Fritzing-Library/blob/master/parts/DHT11%20Humitidy%20and%20Temperature%20Sensor.fzpz
